// Logisim project TP3.circ as structural Verilog
module _1 (
  input  in_1,
  input  in_2,
  input  in_3,
  input  in_4,
  input  in_5,
  output out_6,
  output out_7,
  output out_8
);

  not not_1 (out_6, in_1);
  and and_1 (out_7, in_2, in_3);
  or or_1 (out_8, in_4, in_5);
endmodule

module _2 (
  input  A,
  input  B,
  input  C,
  output out_4
);

  wire and_1_out, and_2_out, and_3_out;

  and and_1 (and_1_out, A, B);
  and and_2 (and_2_out, B, C);
  and and_3 (and_3_out, A, C);
  or or_1 (out_4, and_1_out, and_2_out, and_3_out);
endmodule

module _3 (
  input  x1,
  input  x0,
  output y3,
  output y2,
  output y0
);

  wire not_1_out;

  not not_1 (not_1_out, x0);
  and and_1 (y3, x1, x0);
  and and_2 (y2, x1, not_1_out);

  assign y0 = x0;
endmodule

module _4 (
  input  x2,
  input  x1,
  input  x0,
  output y4,
  output y3,
  output y2,
  output y1,
  output y0
);

  wire and_1_out, and_2_out, and_3_out, and_4_out, and_6_out, and_7_out, not_1_out, not_2_out, not_3_out;

  not not_1 (not_1_out, x2);
  not not_2 (not_2_out, x1);
  not not_3 (not_3_out, x0);
  and and_1 (and_1_out, not_1_out, x1, x0);
  and and_2 (and_2_out, x2, not_2_out, not_2_out);
  and and_3 (and_3_out, x2, x0);
  and and_4 (and_4_out, not_1_out, x1, not_3_out);
  and and_5 (y4, x2, x1);
  and and_6 (and_6_out, x1, not_3_out);
  and and_7 (and_7_out, not_2_out, x0);
  or or_1 (y3, and_1_out, and_2_out);
  or or_2 (y2, and_2_out, and_3_out, and_4_out);
  or or_3 (y1, and_6_out, and_7_out);

  assign y0 = x0;
endmodule

module _5 (
  input  a,
  input  b,
  output fs,
  output fie,
  output fse,
  output fe,
  output fi
);

  wire and_1_out, and_3_out, not_1_out, not_2_out;

  not not_1 (not_1_out, b);
  not not_2 (not_2_out, a);
  and and_1 (and_1_out, a, b);
  and and_2 (fs, a, not_1_out);
  and and_3 (and_3_out, not_2_out, not_1_out);
  or or_1 (fse, and_1_out, not_1_out);
  or or_2 (fie, and_3_out, b);
  or or_3 (fe, and_3_out, and_1_out);
  and and_4 (fi, not_2_out, b);

  // Notes on the sheet:
  //   fs : a > b
  //   fse : a >= b
  //   fie : a <= b
  //   fe : a = b
  //   fi : a < b
  //   5.2   les valeurs de 'fs' et 'fie' sont opposés (car leur somme est 0)
endmodule

module _5_5 (
  input  a1,
  input  a0,
  input  b1,
  input  b0,
  output fi,
  output fie,
  output fse,
  output fe
);

  wire and_1_out, n5_1_fe, n5_2_fe, n5_2_fi, n5_3_fi;

  _5 u_5_1 (.a(a1), .b(b1), .fe(n5_1_fe));  // open: fs, fie, fse, fi
  _5 u_5_2 (.a(a0), .b(b0), .fe(n5_2_fe), .fi(n5_2_fi));  // open: fs, fie, fse
  _5 u_5_3 (.a(a1), .b(b1), .fi(n5_3_fi));  // open: fs, fie, fse, fe
  and and_1 (and_1_out, n5_1_fe, n5_2_fi);
  or or_1 (fi, n5_3_fi, and_1_out);
  not not_1 (fse, fi);
  and and_2 (fe, n5_1_fe, n5_2_fe);
  or or_2 (fie, fi, fe);

  // Notes on the sheet:
  //   fi : A < B
  //   fie : A <= B
  //   fse : A >= B
  //   fe : A = B 
endmodule

module _6 (
  input  in_1,
  input  in_2,
  input  in_3,
  input  in_4,
  input  in_5,
  input  in_6,
  input  in_7,
  input  in_8,
  input  in_9,
  output out_10,
  output out_11,
  output out_12,
  output out_13,
  output out_14
);

  wire nor_1_out, nor_2_out, nor_3_out, nor_4_out, nor_5_out, nor_6_out, nor_7_out, nor_9_out, nor_10_out,
       or_1_out;

  not nor_1 (nor_1_out, in_2);  // NOR_Gate
  not nor_2 (nor_2_out, in_3);  // NOR_Gate
  not nor_3 (nor_3_out, in_6);  // NOR_Gate
  not nor_4 (nor_4_out, in_7);  // NOR_Gate
  nor nor_5 (nor_5_out, in_9, in_8);
  not nor_6 (nor_6_out, in_8);  // NOR_Gate
  not nor_7 (nor_7_out, in_9);  // NOR_Gate
  not nor_8 (out_10, in_1);  // NOR_Gate
  nor nor_9 (nor_9_out, in_4, in_5);
  or or_1 (or_1_out, nor_3_out, nor_4_out);
  nor nor_10 (nor_10_out, nor_6_out, nor_7_out);
  not nor_11 (out_12, nor_9_out);  // NOR_Gate
  buf or_2 (out_13, or_1_out);  // OR_Gate
  nor nor_12 (out_14, nor_5_out, nor_10_out);
  nor nor_13 (out_11, nor_1_out, nor_2_out);
endmodule
