// Logisim project TP4.circ as structural Verilog: 7 circuits, main circuit main
module main (
  input  e1,
  input  e2,
  input  e3,
  output z1,
  output z0,
  output u1,
  output u0
);

  wire and_1_out, and_2_out, and_3_out, and_4_out, and_5_out, and_6_out, and_7_out, not_1_out, not_2_out,
       not_3_out, not_4_out, not_5_out, not_6_out, not_7_out, not_8_out, not_9_out, not_10_out, not_11_out,
       not_12_out;

  not not_1 (not_1_out, e3);
  not not_2 (not_2_out, e1);
  not not_3 (not_3_out, e2);
  not not_4 (not_4_out, e2);
  not not_5 (not_5_out, e3);
  not not_6 (not_6_out, e1);
  not not_7 (not_7_out, e3);
  not not_8 (not_8_out, e1);
  and and_1 (and_1_out, e1, e2, not_1_out);
  not not_9 (not_9_out, e1);
  not not_10 (not_10_out, e2);
  not not_11 (not_11_out, e3);
  not not_12 (not_12_out, e2);
  and and_2 (and_2_out, not_2_out, not_3_out);
  and and_3 (and_3_out, not_4_out, not_5_out);
  and and_4 (and_4_out, not_6_out, not_7_out);
  and and_5 (and_5_out, not_8_out, e2, e3);
  and and_6 (and_6_out, e1, not_12_out, e3);
  and and_7 (and_7_out, not_9_out, not_10_out, not_11_out);
  or or_1 (z0, and_5_out, and_6_out, and_1_out, and_7_out);
  or or_2 (z1, and_2_out, and_3_out, and_4_out);
  not not_13 (u1, z1);
  not not_14 (u0, z0);
endmodule

module _2 (
  input  e3,
  input  e2,
  input  e1,
  input  e0,
  output s3,
  output s2,
  output s1,
  output s0
);

  wire and_2_out, and_3_out, and_4_out, and_5_out, and_6_out, and_7_out, and_8_out, and_9_out, and_10_out,
       and_11_out, and_12_out, not_1_out, not_2_out;

  not not_1 (not_1_out, e0);
  not not_2 (not_2_out, e2);
  and and_1 (s3, e3, e0, e2, e1);
  and and_2 (and_2_out, e3, e2, e1);
  and and_3 (and_3_out, e3, e2, e0);
  and and_4 (and_4_out, e3, e1, e0);
  and and_5 (and_5_out, e2, e1, e0);
  and and_6 (and_6_out, e3, e2);
  and and_7 (and_7_out, e3, e1);
  and and_8 (and_8_out, e3, e0);
  and and_9 (and_9_out, e2, e1);
  and and_10 (and_10_out, e1, e0);
  and and_11 (and_11_out, e2, not_1_out);
  and and_12 (and_12_out, not_2_out, e0);
  or or_1 (s0, e3, and_11_out, and_12_out, e1);
  or or_2 (s2, and_2_out, and_3_out, and_4_out, and_5_out);
  or or_3 (s1, and_6_out, and_7_out, and_8_out, and_9_out, and_10_out);
endmodule

module _3 (
  input  A,
  input  B,
  output S0,
  output S1,
  output S2,
  output S3
);

  wire not_1_out, not_2_out, not_3_out, not_4_out;

  not not_1 (not_1_out, A);
  not not_2 (not_2_out, B);
  not not_3 (not_3_out, A);
  not not_4 (not_4_out, B);
  and and_1 (S0, not_1_out, not_2_out);
  and and_2 (S1, not_3_out, B);
  and and_3 (S2, A, not_4_out);
  and and_4 (S3, B, A);
endmodule

module _4 (
  input  I0,
  input  I1,
  input  I2,
  input  I3,
  input  N1,
  input  N0,
  output S
);

  wire n3_1_s2, n3_2_s2, n3_3_s3, n3_4_s3, n3_5_s2, n3_6_s3, n3_7_s2, n3_8_s3;

  _3 u_3_1 (.A(I0), .B(N1), .S2(n3_1_s2));  // open: S0, S1, S3
  _3 u_3_2 (.A(I1), .B(N1), .S2(n3_2_s2));  // open: S0, S1, S3
  _3 u_3_3 (.A(I2), .B(N1), .S3(n3_3_s3));  // open: S0, S1, S2
  _3 u_3_4 (.A(I3), .S3(n3_4_s3));  // open: B, S0, S1, S2
  _3 u_3_5 (.A(n3_1_s2), .B(N0), .S2(n3_5_s2));  // open: S0, S1, S3
  _3 u_3_6 (.A(n3_2_s2), .B(N0), .S3(n3_6_s3));  // open: S0, S1, S2
  _3 u_3_7 (.A(n3_3_s3), .B(N0), .S2(n3_7_s2));  // open: S0, S1, S3
  _3 u_3_8 (.A(n3_4_s3), .B(N0), .S3(n3_8_s3));  // open: S0, S1, S2
  or or_1 (S, n3_5_s2, n3_6_s3, n3_7_s2, n3_8_s3);
endmodule

module _5 (
  input  n0,
  input  n1,
  input  d,
  output S0,
  output S1,
  output S2,
  output S3
);

  wire n3_1_s0, n3_1_s1, n3_1_s2, n3_1_s3;

  _3 u_3_1 (.A(n0), .B(n1), .S0(n3_1_s0), .S1(n3_1_s1), .S2(n3_1_s2), .S3(n3_1_s3));
  and and_1 (S0, n3_1_s0, d);
  and and_2 (S1, n3_1_s1, d);
  and and_3 (S2, n3_1_s2, d);
  and and_4 (S3, n3_1_s3, d);
endmodule

module _6 (
  input  n,
  input  d0,
  input  d1,
  output S
);

  wire and_1_out, and_2_out, not_1_out;

  not not_1 (not_1_out, n);
  and and_1 (and_1_out, n, d0);
  and and_2 (and_2_out, not_1_out, d1);
  or or_1 (S, and_1_out, and_2_out);
endmodule

module _7 (
  input  d0,
  input  d1,
  input  d2,
  input  d3,
  input  n0,
  input  n1,
  output S0,
  output S1,
  output S2
);

  wire and_1_out, and_2_out, not_1_out, or_1_out, or_2_out;

  Multiplexer multiplexer_1 (.in0(d1), .in1(d0), .out(S0), .sel(or_1_out));  // open: en
  or or_1 (or_1_out, n0, n1);
  and and_1 (and_1_out, not_1_out, n1);
  not not_1 (not_1_out, n0);
  Multiplexer multiplexer_2 (.in0(d2), .in1(d1), .out(S1), .sel(or_2_out));  // open: en
  or or_2 (or_2_out, and_1_out, and_2_out);
  Multiplexer multiplexer_3 (.in0(d3), .in1(d2), .out(S2), .sel(and_2_out));  // open: en
  and and_2 (and_2_out, n0, n1);
endmodule
