// Logisim project TP5-2.0.circ as structural Verilog
module main (
  input  D,
  input  CK,
  output Q
);

  wire and_1_out, and_2_out, nor_1_out, not_1_out;

  not not_1 (not_1_out, CK);
  and and_1 (and_1_out, D, CK);
  and and_2 (and_2_out, CK, not_1_out);
  not nor_1 (nor_1_out, and_1_out);  // NOR_Gate
  nor nor_2 (Q, nor_1_out, and_2_out);
endmodule

module _2 (
  input  CLR
);

  wire and_1_out, clock_1_out;

  Clock clock_1 (.out(clock_1_out));
  and and_1 (and_1_out, CLR, clock_1_out);
  LED led_1 (.in(and_1_out));
endmodule

module _3 (
  input  e1,
  input  e0,
  input  a1,
  input  a0,
  output s1,
  output s0
);

  wire and_1_out, and_2_out, and_3_out, and_4_out, and_5_out, and_6_out, and_7_out, and_8_out, not_1_out,
       not_2_out, not_3_out, not_4_out, not_5_out, not_6_out;

  not not_1 (not_1_out, a1);
  not not_2 (not_2_out, a0);
  not not_3 (not_3_out, a0);
  not not_4 (not_4_out, e1);
  not not_5 (not_5_out, a1);
  not not_6 (not_6_out, a0);
  and and_1 (and_1_out, e1, a0);
  and and_2 (and_2_out, not_4_out, not_5_out, not_6_out);
  and and_3 (and_3_out, e0, a1, a0);
  and and_4 (and_4_out, e1, e0, a1);
  and and_5 (and_5_out, e1, not_1_out);
  and and_6 (and_6_out, e1, not_2_out);
  and and_7 (and_7_out, e1, e0);
  and and_8 (and_8_out, e0, a1, not_3_out);
  or or_1 (s1, and_5_out, and_6_out, and_7_out, and_8_out);
  or or_2 (s0, and_1_out, and_2_out, and_3_out, and_4_out);
endmodule

module _3_2 (
  input  a1,
  input  a0,
  input  CLR,
  output S1,
  output S2
);

  wire and_1_out, and_2_out, clock_1_out, n3_1_s0, n3_1_s1;

  Clock clock_1 (.out(clock_1_out));
  _3 u_3_1 (.e1(S1), .e0(S2), .a1(a1), .a0(a0), .s1(n3_1_s1), .s0(n3_1_s0));
  and and_1 (and_1_out, n3_1_s1, CLR);
  and and_2 (and_2_out, n3_1_s0, CLR);
  D_Flip_Flop d_ff_1 (.clk(and_1_out), .D(clock_1_out), .Q(S1));  // open: Qn, preset, en, reset
  D_Flip_Flop d_ff_2 (.clk(and_2_out), .D(clock_1_out), .Q(S2));  // open: Qn, preset, en, reset
endmodule

module _4 (
  input  A,
  input  P1,
  input  P2,
  input  P3,
  output P1P,
  output P2P,
  output P3P
);

  wire and_1_out, and_2_out, and_3_out, and_4_out, and_5_out, and_6_out, and_7_out, and_8_out, and_9_out,
       not_1_out, not_2_out, not_3_out, not_4_out, not_5_out, not_6_out, not_7_out, not_8_out;

  not not_1 (not_1_out, A);
  not not_2 (not_2_out, P2);
  not not_3 (not_3_out, P3);
  not not_4 (not_4_out, P1);
  not not_5 (not_5_out, A);
  not not_6 (not_6_out, P1);
  not not_7 (not_7_out, P2);
  not not_8 (not_8_out, P3);
  and and_1 (and_1_out, P1, P2, P3);
  and and_2 (and_2_out, P1, not_2_out);
  and and_3 (and_3_out, P1, not_3_out);
  and and_4 (and_4_out, not_6_out, P3);
  and and_5 (and_5_out, not_7_out, P3);
  and and_6 (and_6_out, not_1_out, P1);
  and and_7 (and_7_out, not_4_out, P2, P3);
  and and_8 (and_8_out, not_5_out, P3);
  and and_9 (and_9_out, P2, not_8_out);
  or or_1 (P1P, A, and_1_out);
  or or_2 (P2P, and_6_out, and_2_out, and_3_out, and_7_out);
  or or_3 (P3P, and_8_out, and_4_out, and_5_out, and_9_out);
endmodule
