// Logisim project TP5.circ as structural Verilog: 2 circuits, main circuit main
module main (
  input  D,
  input  CK,
  output out_3,
  output out_4
);

  wire and_1_out, and_2_out, not_1_out;

  not not_1 (not_1_out, CK);
  and and_1 (and_1_out, D, CK);
  and and_2 (and_2_out, CK, not_1_out);
  nor nor_1 (out_3, and_1_out, out_4);
  nor nor_2 (out_4, out_3, and_2_out);
endmodule

module _2 (
  input  CLR
);

  wire and_1_out, clock_1_out;

  Clock clock_1 (.out(clock_1_out));
  and and_1 (and_1_out, CLR, clock_1_out);
  LED led_1 (.in(and_1_out));
endmodule
