// Logisim project test.circ as structural Verilog
module main (
  input  e1,
  input  e2,
  input  e3,
  output z1,
  output z0,
  output u1,
  output u0
);

  wire and_1_out, and_2_out, and_3_out, and_4_out, and_5_out, and_6_out, and_7_out, not_1_out, not_2_out,
       not_3_out, not_4_out, not_5_out, not_6_out, not_7_out, not_8_out, not_9_out, not_10_out, not_11_out,
       not_12_out;

  not not_1 (not_1_out, e3);
  not not_2 (not_2_out, e1);
  not not_3 (not_3_out, e2);
  not not_4 (not_4_out, e2);
  not not_5 (not_5_out, e3);
  not not_6 (not_6_out, e1);
  not not_7 (not_7_out, e3);
  not not_8 (not_8_out, e1);
  and and_1 (and_1_out, e1, e2, not_1_out);
  not not_9 (not_9_out, e1);
  not not_10 (not_10_out, e2);
  not not_11 (not_11_out, e3);
  not not_12 (not_12_out, e2);
  and and_2 (and_2_out, not_2_out, not_3_out);
  and and_3 (and_3_out, not_4_out, not_5_out);
  and and_4 (and_4_out, not_6_out, not_7_out);
  and and_5 (and_5_out, not_8_out, e2, e3);
  and and_6 (and_6_out, e1, not_12_out, e3);
  and and_7 (and_7_out, not_9_out, not_10_out, not_11_out);
  or or_1 (z0, and_5_out, and_6_out, and_1_out, and_7_out);
  or or_2 (z1, and_2_out, and_3_out, and_4_out);
  not not_13 (u1, z1);
  not not_14 (u0, z0);
endmodule

module _2 (
  input  e3,
  input  e2,
  input  e1,
  input  e0,
  output s3,
  output s2,
  output s1,
  output s0
);

  wire and_2_out, and_3_out, and_4_out, and_5_out, and_6_out, and_7_out, and_8_out, and_9_out, and_10_out,
       and_11_out, and_12_out, not_1_out, not_2_out;

  not not_1 (not_1_out, e0);
  not not_2 (not_2_out, e2);
  and and_1 (s3, e3, e0, e2, e1);
  and and_2 (and_2_out, e3, e2, e1);
  and and_3 (and_3_out, e3, e2, e0);
  and and_4 (and_4_out, e3, e1, e0);
  and and_5 (and_5_out, e2, e1, e0);
  and and_6 (and_6_out, e3, e2);
  and and_7 (and_7_out, e3, e1);
  and and_8 (and_8_out, e3, e0);
  and and_9 (and_9_out, e2, e1);
  and and_10 (and_10_out, e1, e0);
  and and_11 (and_11_out, e2, not_1_out);
  and and_12 (and_12_out, not_2_out, e0);
  or or_1 (s0, e3, and_11_out, and_12_out, e1);
  or or_2 (s2, and_2_out, and_3_out, and_4_out, and_5_out);
  or or_3 (s1, and_6_out, and_7_out, and_8_out, and_9_out, and_10_out);
endmodule

module _3 (
  input  A,
  input  B,
  output S0,
  output S1,
  output S2,
  output S3
);

  wire not_1_out, not_2_out, not_3_out, not_4_out;

  not not_1 (not_1_out, A);
  not not_2 (not_2_out, B);
  not not_3 (not_3_out, A);
  not not_4 (not_4_out, B);
  and and_1 (S0, not_1_out, not_2_out);
  and and_2 (S1, not_3_out, B);
  and and_3 (S2, A, not_4_out);
  and and_4 (S3, B, A);
endmodule
